// Logisim project LogisimTemplate.circ as structural Verilog: 1 circuit, main circuit main
module main (
  input  X1,
  input  X2,
  input  X3,
  input  X4,
  output Z1,
  output Z2
);

  wire not_1_out, not_2_out, not_3_out, not_4_out;

  // OR_Gate or_1 is placed but not wired
  // AND_Gate and_1 is placed but not wired
  // AND_Gate and_2 is placed but not wired
  // AND_Gate and_3 is placed but not wired
  // AND_Gate and_4 is placed but not wired
  not not_1 (not_1_out, X1);
  not not_2 (not_2_out, X2);
  not not_3 (not_3_out, X3);
  not not_4 (not_4_out, X4);
  // AND_Gate and_5 is placed but not wired
  // AND_Gate and_6 is placed but not wired
  // AND_Gate and_7 is placed but not wired
  // AND_Gate and_8 is placed but not wired
  // OR_Gate or_2 is placed but not wired

  // Notes on the sheet:
  //   Output 1
  //   ........
  //   Inputs X1, X2, X3 & X4
  //   ........
  //   Output 2
endmodule
