// Logisim project Adder_CIRCUIT.circ as structural Verilog: 2 circuits, main circuit main
module main (
  input  in_1,
  input  in_2,
  input  in_3,
  input  in_4,
  input  X0,
  input  in_6,
  input  in_7,
  input  Y0,
  input  in_9,
  input  in_10,
  input  in_11,
  input  in_12,
  input  X1,
  input  Y1,
  input  in_15,
  input  in_16,
  input  x2,
  input  Y2,
  input  X3,
  input  Y3,
  input  in_21,
  input  in_22,
  input  in_23,
  input  A,
  input  B,
  input  C,
  output out_27
);

  wire adder_1_cout, adder_1_out, adder_2_cout, adder_2_out, adder_3_cout, adder_3_out, adder_4_cout,
       adder_4_out, and_1_out, and_2_out, and_3_out, and_4_out, and_5_out, and_6_out, and_7_out, and_8_out,
       and_9_out, and_10_out, not_1_out, not_2_out, not_3_out, or_1_out, or_2_out, or_3_out, xor_1_out,
       xor_2_out, xor_3_out, xor_4_out, xor_5_out, xor_6_out, xor_7_out, xor_8_out, xor_9_out, xor_10_out,
       xor_11_out;

  xor xor_1 (xor_1_out, in_1, in_2);
  and and_1 (and_1_out, in_1, in_2);
  LED led_1 (.in(and_1_out));
  LED led_2 (.in(xor_1_out));
  Xor_imple xor_imple_1 (.A(in_15), .B(in_16), .F(out_27));
  Adder #(.width(1)) adder_1 (.a(in_3), .b(in_4), .out(adder_1_out), .cin(1'b0), .cout(adder_1_cout));
  Adder #(.width(1)) adder_2 (.a(in_6), .b(in_7), .out(adder_2_out), .cin(adder_1_cout), .cout(adder_2_cout));
  Adder #(.width(1)) adder_3 (.a(in_9), .b(in_10), .out(adder_3_out), .cin(adder_2_cout), .cout(adder_3_cout));
  Adder #(.width(1)) adder_4 (.a(in_11), .b(in_12), .out(adder_4_out), .cin(adder_3_cout), .cout(adder_4_cout));
  LED led_3 (.in(adder_4_cout));
  LED led_4 (.in(adder_4_out));
  LED led_5 (.in(adder_3_out));
  LED led_6 (.in(adder_2_out));
  LED led_7 (.in(adder_1_out));
  and and_2 (and_2_out, in_21, in_22, in_23);
  xor xor_2 (xor_2_out, A, B);
  xor xor_3 (xor_3_out, C, A);
  xor xor_4 (xor_4_out, C, B);
  not not_1 (not_1_out, xor_2_out);
  not not_2 (not_2_out, xor_3_out);
  not not_3 (not_3_out, xor_4_out);
  xor xor_5 (xor_5_out, X1, Y1);
  and and_3 (and_3_out, X1, Y1);
  xor xor_6 (xor_6_out, x2, Y2);
  and and_4 (and_4_out, x2, Y2);
  xor xor_7 (xor_7_out, X3, Y3);
  and and_5 (and_5_out, X3, Y3);
  LED led_8 (.in(and_2_out));
  and and_6 (and_6_out, not_1_out, not_2_out, not_3_out);
  LED led_9 (.in(and_6_out));
  xor xor_8 (xor_8_out, X0, Y0);
  and and_7 (and_7_out, X0, Y0);
  xor xor_9 (xor_9_out, and_7_out, xor_5_out);
  and and_8 (and_8_out, and_7_out, xor_5_out);
  xor xor_10 (xor_10_out, or_1_out, xor_6_out);
  and and_9 (and_9_out, or_1_out, xor_6_out);
  xor xor_11 (xor_11_out, or_2_out, xor_7_out);
  and and_10 (and_10_out, or_2_out, xor_7_out);
  or or_1 (or_1_out, and_8_out, and_3_out);
  or or_2 (or_2_out, and_9_out, and_4_out);
  or or_3 (or_3_out, and_10_out, and_5_out);
  LED led_10 (.in(or_3_out));
  LED led_11 (.in(xor_11_out));
  LED led_12 (.in(xor_10_out));
  LED Sum (.in(xor_9_out));
  LED led_13 (.in(xor_8_out));
endmodule

module Xor_imple (
  input  A,
  input  B,
  output F
);

  xor xor_1 (F, A, B);
endmodule
