// Logisim project STAGE2.circ as structural Verilog: 2 circuits, main circuit main
module main (
);

  wire and_1_out, button_1_out, clock_1_out, t_ff_1_q;
  wire [3:0] bcd_counter_1_a0;

  Hex_Digit_Display hex_digit_display_1 ();  // open: value, dp
  Hex_Digit_Display hex_digit_display_2 ();  // open: value, dp
  Button button_1 (.out(button_1_out));
  Hex_Digit_Display hex_digit_display_3 (.value(4'b0000));  // open: dp
  Hex_Digit_Display hex_digit_display_4 (.value(bcd_counter_1_a0));  // open: dp
  Button button_2 ();  // open: out
  Button button_3 ();  // open: out
  Hex_Digit_Display hex_digit_display_5 ();  // open: value, dp
  Hex_Digit_Display hex_digit_display_6 ();  // open: value, dp
  bcd_counter bcd_counter_1 (
    .clockInput(and_1_out), .A3(bcd_counter_1_a0[3]), .A2(bcd_counter_1_a0[2]), .A1(bcd_counter_1_a0[1]),
    .A0(bcd_counter_1_a0[0]));  // open: oneCycle
  Hex_Digit_Display hex_digit_display_7 ();  // open: value, dp
  LED led_1 (.in(t_ff_1_q));
  Hex_Digit_Display hex_digit_display_8 ();  // open: value, dp
  T_Flip_Flop t_ff_1 (.T(button_1_out), .clk(button_1_out), .Q(t_ff_1_q));  // open: Qn, reset, preset
  Clock clock_1 (.out(clock_1_out));
  and and_1 (and_1_out, clock_1_out, t_ff_1_q);

  // Notes on the sheet:
  //   Elapsed Time
  //   Minutes
  //   :
  //   Start / Stop
  //   Seconds
  //   Stopwatch Interface
  //   Split
  //   Reset
  //   Minutes
  //   Clock Started
  //   Split Time
  //   :
  //   Seconds
endmodule

module bcd_counter (
  input  clockInput,
  output A3,
  output A2,
  output A1,
  output A0,
  output oneCycle
);

  wire and_1_out, and_3_out;

  LED led_1 (.in(A3));
  LED led_2 (.in(A2));
  T_Flip_Flop T0 (.T(1'b1), .clk(clockInput), .Q(A0), .reset(oneCycle));  // open: Qn, preset
  LED led_3 (.in(A1));
  T_Flip_Flop T1 (.T(A0), .clk(clockInput), .Q(A1), .reset(oneCycle));  // open: Qn, preset
  LED led_4 (.in(A0));
  and and_1 (and_1_out, A0, A1);
  and and_2 (oneCycle, A1, A3);
  T_Flip_Flop T2 (.T(and_1_out), .clk(clockInput), .Q(A2), .reset(oneCycle));  // open: Qn, preset
  and and_3 (and_3_out, and_1_out, A2);
  T_Flip_Flop T3 (.T(and_3_out), .clk(clockInput), .Q(A3), .reset(oneCycle));  // open: Qn, preset
  Hex_Digit_Display hex_digit_display_1 (.value({A3, A2, A1, A0}));  // open: dp
endmodule
