// Logisim project STAGE3.circ as structural Verilog: 3 circuits, main circuit main
module main (
);

  wire and_1_out, and_2_out, bcd_counter_1_onecycle, button_1_out, button_3_out, clock_1_out, or_1_out,
       t_ff_1_q, uptofivecounter_1_onecycle;
  wire [3:0] bcd_counter_1_a0, uptofivecounter_1_a0;

  Hex_Digit_Display hex_digit_display_1 ();  // open: value, dp
  Hex_Digit_Display hex_digit_display_2 ();  // open: value, dp
  Button button_1 (.out(button_1_out));
  Hex_Digit_Display hex_digit_display_3 (.value(uptofivecounter_1_a0));  // open: dp
  Hex_Digit_Display hex_digit_display_4 (.value(bcd_counter_1_a0));  // open: dp
  Button button_2 ();  // open: out
  Button button_3 (.out(button_3_out));
  Hex_Digit_Display hex_digit_display_5 ();  // open: value, dp
  Hex_Digit_Display hex_digit_display_6 ();  // open: value, dp
  bcd_counter bcd_counter_1 (
    .clockInput(and_2_out), .resetPin(button_3_out), .A3(bcd_counter_1_a0[3]), .A2(bcd_counter_1_a0[2]),
    .A1(bcd_counter_1_a0[1]), .A0(bcd_counter_1_a0[0]), .oneCycle(bcd_counter_1_onecycle));
  UptoFiveCounter uptofivecounter_1 (
    .clockInput(bcd_counter_1_onecycle), .resetPin(button_3_out), .A3(uptofivecounter_1_a0[3]),
    .A2(uptofivecounter_1_a0[2]), .A1(uptofivecounter_1_a0[1]), .A0(uptofivecounter_1_a0[0]),
    .oneCycle(uptofivecounter_1_onecycle));
  Hex_Digit_Display hex_digit_display_7 ();  // open: value, dp
  LED led_1 (.in(t_ff_1_q));
  Hex_Digit_Display hex_digit_display_8 ();  // open: value, dp
  and and_1 (and_1_out, t_ff_1_q, button_3_out);
  T_Flip_Flop t_ff_1 (.T(or_1_out), .clk(or_1_out), .Q(t_ff_1_q));  // open: Qn, reset, preset
  or or_1 (or_1_out, and_1_out, button_1_out);
  Clock clock_1 (.out(clock_1_out));
  and and_2 (and_2_out, t_ff_1_q, clock_1_out);

  // Notes on the sheet:
  //   Elapsed Time
  //   Minutes
  //   :
  //   Start / Stop
  //   Seconds
  //   Stopwatch Interface
  //   Split
  //   Reset
  //   Minutes
  //   Clock Started
  //   Split Time
  //   :
  //   Seconds
endmodule

module bcd_counter (
  input  clockInput,
  input  resetPin,
  output A3,
  output A2,
  output A1,
  output A0,
  output oneCycle
);

  wire and_1_out, and_2_out, and_3_out;

  and and_1 (and_1_out, A1, A3);
  LED led_1 (.in(A3));
  LED led_2 (.in(A2));
  T_Flip_Flop t_ff_1 (.T(1'b1), .clk(clockInput), .Q(A0), .reset(oneCycle));  // open: Qn, preset
  LED led_3 (.in(A1));
  T_Flip_Flop t_ff_2 (.T(A0), .clk(clockInput), .Q(A1), .reset(oneCycle));  // open: Qn, preset
  or or_1 (oneCycle, resetPin, and_1_out);
  LED led_4 (.in(A0));
  and and_2 (and_2_out, A0, A1);
  T_Flip_Flop t_ff_3 (.T(and_2_out), .clk(clockInput), .Q(A2), .reset(oneCycle));  // open: Qn, preset
  and and_3 (and_3_out, and_2_out, A2);
  T_Flip_Flop t_ff_4 (.T(and_3_out), .clk(clockInput), .Q(A3), .reset(oneCycle));  // open: Qn, preset
  Hex_Digit_Display hex_digit_display_1 (.value({A3, A2, A1, A0}));  // open: dp
endmodule

module UptoFiveCounter (
  input  clockInput,
  input  resetPin,
  output A3,
  output A2,
  output A1,
  output A0,
  output oneCycle
);

  wire and_1_out, and_2_out, not_1_out;

  and and_1 (and_1_out, not_1_out, A1, A2);
  not not_1 (not_1_out, A0);
  or or_1 (oneCycle, and_1_out, resetPin);
  T_Flip_Flop t_ff_1 (.T(1'b1), .clk(clockInput), .Q(A0), .reset(oneCycle));  // open: Qn, preset
  LED led_1 (.in(A2));
  LED led_2 (.in(A1));
  T_Flip_Flop t_ff_2 (.T(A0), .clk(clockInput), .Q(A1), .reset(oneCycle));  // open: Qn, preset
  LED led_3 (.in(A0));
  and and_2 (and_2_out, A0, A1);
  T_Flip_Flop t_ff_3 (.T(and_2_out), .clk(clockInput), .Q(A2), .reset(oneCycle));  // open: Qn, preset
  Hex_Digit_Display hex_digit_display_1 (.value({1'b0, A2, A1, A0}));  // open: dp

  assign A3 = 1'b0;
endmodule
