// Logisim project STAGE4.circ as structural Verilog: 5 circuits, main circuit main
module main (
);

  wire button_1_out, button_3_out, controlunit_1_clockout, controlunit_1_resetout, controlunit_1_watchstate;
  wire [3:0] elapsedtimedisplay_1_minutelsd, elapsedtimedisplay_1_minutemsd, elapsedtimedisplay_1_secondlsd,
       elapsedtimedisplay_1_secondmsd;

  Hex_Digit_Display hex_digit_display_1 (.value(elapsedtimedisplay_1_minutemsd));  // open: dp
  Hex_Digit_Display hex_digit_display_2 (.value(elapsedtimedisplay_1_minutelsd));  // open: dp
  Button button_1 (.out(button_1_out));
  Hex_Digit_Display hex_digit_display_3 (.value(elapsedtimedisplay_1_secondmsd));  // open: dp
  Hex_Digit_Display hex_digit_display_4 (.value(elapsedtimedisplay_1_secondlsd));  // open: dp
  Button button_2 ();  // open: out
  ElapsedTimeDisplay elapsedtimedisplay_1 (
    .ClockInput(controlunit_1_clockout), .ResetInput(controlunit_1_resetout),
    .SecondLSD(elapsedtimedisplay_1_secondlsd), .SecondMSD(elapsedtimedisplay_1_secondmsd),
    .MinuteLSD(elapsedtimedisplay_1_minutelsd), .MinuteMSD(elapsedtimedisplay_1_minutemsd));
  Button button_3 (.out(button_3_out));
  Hex_Digit_Display hex_digit_display_5 ();  // open: value, dp
  Hex_Digit_Display hex_digit_display_6 ();  // open: value, dp
  Hex_Digit_Display hex_digit_display_7 ();  // open: value, dp
  LED led_1 (.in(controlunit_1_watchstate));
  Hex_Digit_Display hex_digit_display_8 ();  // open: value, dp
  ControlUnit controlunit_1 (
    .StartStop(button_1_out), .ResetIn(button_3_out), .ClockOut(controlunit_1_clockout),
    .WatchState(controlunit_1_watchstate), .ResetOut(controlunit_1_resetout));  // open: SplitIn

  // Notes on the sheet:
  //   Elapsed Time
  //   Minutes
  //   :
  //   Start / Stop
  //   Seconds
  //   Stopwatch Interface
  //   Split
  //   Reset
  //   Minutes
  //   Clock Started
  //   Split Time
  //   :
  //   Seconds
endmodule

module bcd_counter (
  input  clockInput,
  input  resetPin,
  output A3,
  output A2,
  output A1,
  output A0,
  output oneCycle
);

  wire and_1_out, and_2_out, and_3_out;

  and and_1 (and_1_out, A1, A3);
  LED led_1 (.in(A3));
  LED led_2 (.in(A2));
  T_Flip_Flop t_ff_1 (.T(1'b1), .clk(clockInput), .Q(A0), .reset(oneCycle));  // open: Qn, preset
  LED led_3 (.in(A1));
  T_Flip_Flop t_ff_2 (.T(A0), .clk(clockInput), .Q(A1), .reset(oneCycle));  // open: Qn, preset
  or or_1 (oneCycle, resetPin, and_1_out);
  LED led_4 (.in(A0));
  and and_2 (and_2_out, A0, A1);
  T_Flip_Flop t_ff_3 (.T(and_2_out), .clk(clockInput), .Q(A2), .reset(oneCycle));  // open: Qn, preset
  and and_3 (and_3_out, and_2_out, A2);
  T_Flip_Flop t_ff_4 (.T(and_3_out), .clk(clockInput), .Q(A3), .reset(oneCycle));  // open: Qn, preset
  Hex_Digit_Display hex_digit_display_1 (.value({A3, A2, A1, A0}));  // open: dp
endmodule

module UptoFiveCounter (
  input  clockInput,
  input  resetPin,
  output A3,
  output A2,
  output A1,
  output A0,
  output oneCycle
);

  wire and_1_out, and_2_out, not_1_out;

  and and_1 (and_1_out, not_1_out, A1, A2);
  not not_1 (not_1_out, A0);
  or or_1 (oneCycle, and_1_out, resetPin);
  T_Flip_Flop t_ff_1 (.T(1'b1), .clk(clockInput), .Q(A0), .reset(oneCycle));  // open: Qn, preset
  LED led_1 (.in(A2));
  LED led_2 (.in(A1));
  T_Flip_Flop t_ff_2 (.T(A0), .clk(clockInput), .Q(A1), .reset(oneCycle));  // open: Qn, preset
  LED led_3 (.in(A0));
  and and_2 (and_2_out, A0, A1);
  T_Flip_Flop t_ff_3 (.T(and_2_out), .clk(clockInput), .Q(A2), .reset(oneCycle));  // open: Qn, preset
  Hex_Digit_Display hex_digit_display_1 (.value({1'b0, A2, A1, A0}));  // open: dp

  assign A3 = 1'b0;
endmodule

module ControlUnit (
  input  StartStop,
  input  ResetIn,
  input  SplitIn,
  output ClockOut,
  output WatchState,
  output ResetOut
);

  wire and_1_out, clock_1_out, or_1_out;

  and and_1 (and_1_out, ResetIn, WatchState);
  or or_1 (or_1_out, StartStop, and_1_out);
  T_Flip_Flop t_ff_1 (.T(or_1_out), .clk(or_1_out), .Q(WatchState));  // open: Qn, reset, preset
  Clock clock_1 (.out(clock_1_out));
  and and_2 (ClockOut, clock_1_out, WatchState);

  assign ResetOut = ResetIn;
endmodule

module ElapsedTimeDisplay (
  input  ClockInput,
  input  ResetInput,
  output [3:0] SecondLSD,
  output [3:0] SecondMSD,
  output [3:0] MinuteLSD,
  output [3:0] MinuteMSD
);

  wire bcd_counter_1_onecycle, bcd_counter_2_onecycle, uptofivecounter_1_onecycle;

  bcd_counter bcd_counter_1 (
    .clockInput(ClockInput), .resetPin(ResetInput), .A3(SecondLSD[3]), .A2(SecondLSD[2]), .A1(SecondLSD[1]),
    .A0(SecondLSD[0]), .oneCycle(bcd_counter_1_onecycle));
  UptoFiveCounter uptofivecounter_1 (
    .clockInput(bcd_counter_1_onecycle), .resetPin(ResetInput), .A3(SecondMSD[3]), .A2(SecondMSD[2]),
    .A1(SecondMSD[1]), .A0(SecondMSD[0]), .oneCycle(uptofivecounter_1_onecycle));
  bcd_counter bcd_counter_2 (
    .clockInput(uptofivecounter_1_onecycle), .resetPin(ResetInput), .A3(MinuteLSD[3]), .A2(MinuteLSD[2]),
    .A1(MinuteLSD[1]), .A0(MinuteLSD[0]), .oneCycle(bcd_counter_2_onecycle));
  bcd_counter bcd_counter_3 (
    .clockInput(bcd_counter_2_onecycle), .resetPin(ResetInput), .A3(MinuteMSD[3]), .A2(MinuteMSD[2]),
    .A1(MinuteMSD[1]), .A0(MinuteMSD[0]));  // open: oneCycle
endmodule
