// Logisim project STAGE6B.circ as structural Verilog: 8 circuits, main circuit main
module main (
);

  wire button_1_out, button_2_out, button_3_out, controlunit_1_clockout, controlunit_1_resetout,
       controlunit_1_splitout, controlunit_1_watchstate, controlunit_1_wrapout, splitimedisplay_1_clockout,
       splitimedisplay_2_clockout;
  wire [3:0] digitchooser_1_outdigit, digitchooser_2_outdigit, digitchooser_3_outdigit,
       digitchooser_4_outdigit, elapsedtimedisplay_1_minutelsd, elapsedtimedisplay_1_minutemsd,
       elapsedtimedisplay_1_secondlsd, elapsedtimedisplay_1_secondmsd, splitimedisplay_1_minutelsddisplay,
       splitimedisplay_1_minutelsdpass, splitimedisplay_1_minutemsdpass, splitimedisplay_1_minutmsddisplay,
       splitimedisplay_1_passsecondlsd, splitimedisplay_1_passsecondmsd, splitimedisplay_1_secondlsddisplay,
       splitimedisplay_1_secondmsddisplay, splitimedisplay_2_minutelsddisplay,
       splitimedisplay_2_minutelsdpass, splitimedisplay_2_minutemsdpass, splitimedisplay_2_minutmsddisplay,
       splitimedisplay_2_passsecondlsd, splitimedisplay_2_passsecondmsd, splitimedisplay_2_secondlsddisplay,
       splitimedisplay_2_secondmsddisplay, splitimedisplay_3_minutelsddisplay,
       splitimedisplay_3_minutmsddisplay, splitimedisplay_3_secondlsddisplay,
       splitimedisplay_3_secondmsddisplay;

  Hex_Digit_Display hex_digit_display_1 (.value(elapsedtimedisplay_1_minutemsd));  // open: dp
  Hex_Digit_Display hex_digit_display_2 (.value(elapsedtimedisplay_1_minutelsd));  // open: dp
  Button button_1 (.out(button_1_out));
  Hex_Digit_Display hex_digit_display_3 (.value(elapsedtimedisplay_1_secondmsd));  // open: dp
  Hex_Digit_Display hex_digit_display_4 (.value(elapsedtimedisplay_1_secondlsd));  // open: dp
  Button button_2 (.out(button_2_out));
  ElapsedTimeDisplay elapsedtimedisplay_1 (
    .ClockInput(controlunit_1_clockout), .ResetInput(controlunit_1_resetout),
    .SecondLSD(elapsedtimedisplay_1_secondlsd), .SecondMSD(elapsedtimedisplay_1_secondmsd),
    .MinuteLSD(elapsedtimedisplay_1_minutelsd), .MinuteMSD(elapsedtimedisplay_1_minutemsd));
  Button button_3 (.out(button_3_out));
  Hex_Digit_Display hex_digit_display_5 (.value(splitimedisplay_1_minutmsddisplay));  // open: dp
  Hex_Digit_Display hex_digit_display_6 (.value(splitimedisplay_1_minutelsddisplay));  // open: dp
  digitChooser digitchooser_1 (
    .watchState(controlunit_1_watchstate), .startDigit(elapsedtimedisplay_1_secondlsd),
    .stopDigit(splitimedisplay_3_secondlsddisplay), .wrap(controlunit_1_wrapout),
    .outDigit(digitchooser_1_outdigit));
  digitChooser digitchooser_2 (
    .watchState(controlunit_1_watchstate), .startDigit(elapsedtimedisplay_1_secondmsd),
    .stopDigit(splitimedisplay_3_secondmsddisplay), .wrap(controlunit_1_wrapout),
    .outDigit(digitchooser_2_outdigit));
  digitChooser digitchooser_3 (
    .watchState(controlunit_1_watchstate), .startDigit(elapsedtimedisplay_1_minutelsd),
    .stopDigit(splitimedisplay_3_minutelsddisplay), .wrap(controlunit_1_wrapout),
    .outDigit(digitchooser_3_outdigit));
  digitChooser digitchooser_4 (
    .watchState(controlunit_1_watchstate), .startDigit(elapsedtimedisplay_1_minutemsd),
    .stopDigit(splitimedisplay_3_minutmsddisplay), .wrap(controlunit_1_wrapout),
    .outDigit(digitchooser_4_outdigit));
  Hex_Digit_Display hex_digit_display_7 (.value(splitimedisplay_1_secondmsddisplay));  // open: dp
  LED led_1 (.in(controlunit_1_watchstate));
  Hex_Digit_Display hex_digit_display_8 (.value(splitimedisplay_1_secondlsddisplay));  // open: dp
  SpliTimeDisplay splitimedisplay_1 (
    .ClockIn(controlunit_1_splitout), .SeondLSDIN(digitchooser_1_outdigit),
    .SecondMSDIn(digitchooser_2_outdigit), .MinuteLSDIn(digitchooser_3_outdigit),
    .MinuteMSDIN(digitchooser_4_outdigit), .ResetPin(controlunit_1_resetout),
    .SecondLSDDisplay(splitimedisplay_1_secondlsddisplay),
    .SecondMSDDisplay(splitimedisplay_1_secondmsddisplay),
    .MinuteLSDDisplay(splitimedisplay_1_minutelsddisplay),
    .MinutMSDDisplay(splitimedisplay_1_minutmsddisplay), .PassSecondLSD(splitimedisplay_1_passsecondlsd),
    .PassSecondMSD(splitimedisplay_1_passsecondmsd), .MinuteLSDPass(splitimedisplay_1_minutelsdpass),
    .MinuteMSDPass(splitimedisplay_1_minutemsdpass), .ClockOut(splitimedisplay_1_clockout));
  ControlUnit controlunit_1 (
    .StartStop(button_1_out), .ResetIn(button_3_out), .SplitIn(button_2_out),
    .ClockOut(controlunit_1_clockout), .WatchState(controlunit_1_watchstate),
    .ResetOut(controlunit_1_resetout), .SplitOut(controlunit_1_splitout), .wrapOut(controlunit_1_wrapout));
  Hex_Digit_Display hex_digit_display_9 (.value(splitimedisplay_1_minutemsdpass));  // open: dp
  Hex_Digit_Display hex_digit_display_10 (.value(splitimedisplay_1_minutelsdpass));  // open: dp
  Hex_Digit_Display hex_digit_display_11 (.value(splitimedisplay_1_passsecondmsd));  // open: dp
  Hex_Digit_Display hex_digit_display_12 (.value(splitimedisplay_1_passsecondlsd));  // open: dp
  Hex_Digit_Display hex_digit_display_13 (.value(splitimedisplay_2_minutmsddisplay));  // open: dp
  SpliTimeDisplay splitimedisplay_2 (
    .ClockIn(splitimedisplay_1_clockout), .SeondLSDIN(splitimedisplay_1_passsecondlsd),
    .SecondMSDIn(splitimedisplay_1_passsecondmsd), .MinuteLSDIn(splitimedisplay_1_minutelsdpass),
    .MinuteMSDIN(splitimedisplay_1_minutemsdpass), .ResetPin(controlunit_1_resetout),
    .SecondLSDDisplay(splitimedisplay_2_secondlsddisplay),
    .SecondMSDDisplay(splitimedisplay_2_secondmsddisplay),
    .MinuteLSDDisplay(splitimedisplay_2_minutelsddisplay),
    .MinutMSDDisplay(splitimedisplay_2_minutmsddisplay), .PassSecondLSD(splitimedisplay_2_passsecondlsd),
    .PassSecondMSD(splitimedisplay_2_passsecondmsd), .MinuteLSDPass(splitimedisplay_2_minutelsdpass),
    .MinuteMSDPass(splitimedisplay_2_minutemsdpass), .ClockOut(splitimedisplay_2_clockout));
  Hex_Digit_Display hex_digit_display_14 (.value(splitimedisplay_2_minutelsddisplay));  // open: dp
  Hex_Digit_Display hex_digit_display_15 (.value(splitimedisplay_2_secondmsddisplay));  // open: dp
  Hex_Digit_Display hex_digit_display_16 (.value(splitimedisplay_2_secondlsddisplay));  // open: dp
  Hex_Digit_Display hex_digit_display_17 (.value(splitimedisplay_2_minutemsdpass));  // open: dp
  Hex_Digit_Display hex_digit_display_18 (.value(splitimedisplay_2_minutelsdpass));  // open: dp
  Hex_Digit_Display hex_digit_display_19 (.value(splitimedisplay_2_passsecondmsd));  // open: dp
  Hex_Digit_Display hex_digit_display_20 (.value(splitimedisplay_2_passsecondlsd));  // open: dp
  SpliTimeDisplay splitimedisplay_3 (
    .ClockIn(splitimedisplay_2_clockout), .SeondLSDIN(splitimedisplay_2_passsecondlsd),
    .SecondMSDIn(splitimedisplay_2_passsecondmsd), .MinuteLSDIn(splitimedisplay_2_minutelsdpass),
    .MinuteMSDIN(splitimedisplay_2_minutemsdpass), .ResetPin(controlunit_1_resetout),
    .SecondLSDDisplay(splitimedisplay_3_secondlsddisplay),
    .SecondMSDDisplay(splitimedisplay_3_secondmsddisplay),
    .MinuteLSDDisplay(splitimedisplay_3_minutelsddisplay), .MinutMSDDisplay(splitimedisplay_3_minutmsddisplay));  // open: PassSecondLSD, PassSecondMSD, MinuteLSDPass, MinuteMSDPass, ClockOut
  Hex_Digit_Display hex_digit_display_21 (.value(splitimedisplay_3_minutmsddisplay));  // open: dp
  Hex_Digit_Display hex_digit_display_22 (.value(splitimedisplay_3_minutelsddisplay));  // open: dp
  Hex_Digit_Display hex_digit_display_23 (.value(splitimedisplay_3_secondmsddisplay));  // open: dp
  Hex_Digit_Display hex_digit_display_24 (.value(splitimedisplay_3_secondlsddisplay));  // open: dp

  // Notes on the sheet:
  //   Elapsed Time
  //   Minutes
  //   :
  //   Start / Stop
  //   Seconds
  //   Stopwatch Interface
  //   Split
  //   Reset
  //   Minutes
  //   Clock Started
  //   Split Time
  //   :
  //   Seconds
  //   Minutes
  //   Split Time
  //   Seconds
  //   :
  //   Minutes
  //   Split Time
  //   :
  //   Seconds
  //   Split Time
  //   Minutes
  //   :
  //   Seconds
  //   Minutes
  //   Split Time
  //   Seconds
  //   :
endmodule

module bcd_counter (
  input  clockInput,
  input  resetPin,
  output A3,
  output A2,
  output A1,
  output A0,
  output oneCycle
);

  wire and_1_out, and_2_out, and_3_out;

  and and_1 (and_1_out, A1, A3);
  LED led_1 (.in(A3));
  LED led_2 (.in(A2));
  T_Flip_Flop t_ff_1 (.T(1'b1), .clk(clockInput), .Q(A0), .reset(oneCycle));  // open: Qn, preset
  LED led_3 (.in(A1));
  T_Flip_Flop t_ff_2 (.T(A0), .clk(clockInput), .Q(A1), .reset(oneCycle));  // open: Qn, preset
  or or_1 (oneCycle, resetPin, and_1_out);
  LED led_4 (.in(A0));
  and and_2 (and_2_out, A0, A1);
  T_Flip_Flop t_ff_3 (.T(and_2_out), .clk(clockInput), .Q(A2), .reset(oneCycle));  // open: Qn, preset
  and and_3 (and_3_out, and_2_out, A2);
  T_Flip_Flop t_ff_4 (.T(and_3_out), .clk(clockInput), .Q(A3), .reset(oneCycle));  // open: Qn, preset
  Hex_Digit_Display hex_digit_display_1 (.value({A3, A2, A1, A0}));  // open: dp
endmodule

module UptoFiveCounter (
  input  clockInput,
  input  resetPin,
  output A3,
  output A2,
  output A1,
  output A0,
  output oneCycle
);

  wire and_1_out, and_2_out, not_1_out;

  and and_1 (and_1_out, not_1_out, A1, A2);
  not not_1 (not_1_out, A0);
  or or_1 (oneCycle, and_1_out, resetPin);
  T_Flip_Flop t_ff_1 (.T(1'b1), .clk(clockInput), .Q(A0), .reset(oneCycle));  // open: Qn, preset
  LED led_1 (.in(A2));
  LED led_2 (.in(A1));
  T_Flip_Flop t_ff_2 (.T(A0), .clk(clockInput), .Q(A1), .reset(oneCycle));  // open: Qn, preset
  LED led_3 (.in(A0));
  and and_2 (and_2_out, A0, A1);
  T_Flip_Flop t_ff_3 (.T(and_2_out), .clk(clockInput), .Q(A2), .reset(oneCycle));  // open: Qn, preset
  Hex_Digit_Display hex_digit_display_1 (.value({1'b0, A2, A1, A0}));  // open: dp

  assign A3 = 1'b0;
endmodule

module ControlUnit (
  input  StartStop,
  input  ResetIn,
  input  SplitIn,
  output ClockOut,
  output WatchState,
  output ResetOut,
  output SplitOut,
  output wrapOut
);

  wire and_1_out, and_2_out, and_4_out, clock_1_out, not_1_out, or_1_out;

  and and_1 (and_1_out, ResetIn, WatchState);
  or or_1 (or_1_out, StartStop, and_1_out);
  T_Flip_Flop t_ff_1 (.T(or_1_out), .clk(or_1_out), .Q(WatchState));  // open: Qn, reset, preset
  Clock clock_1 (.out(clock_1_out));
  not not_1 (not_1_out, WatchState);
  and and_2 (and_2_out, WatchState, SplitIn);
  and and_3 (ClockOut, clock_1_out, WatchState);
  or or_2 (SplitOut, ResetIn, not_1_out, and_2_out);
  and and_4 (and_4_out, not_1_out, SplitIn);
  or or_3 (wrapOut, SplitIn, and_4_out);

  assign ResetOut = ResetIn;
endmodule

module ElapsedTimeDisplay (
  input  ClockInput,
  input  ResetInput,
  output [3:0] SecondLSD,
  output [3:0] SecondMSD,
  output [3:0] MinuteLSD,
  output [3:0] MinuteMSD
);

  wire bcd_counter_1_onecycle, bcd_counter_2_onecycle, buffer_1_out, buffer_2_out, buffer_3_out,
       uptofivecounter_1_onecycle;

  buf buffer_1 (buffer_1_out, ResetInput);
  buf buffer_2 (buffer_2_out, buffer_1_out);
  buf buffer_3 (buffer_3_out, buffer_2_out);
  bcd_counter bcd_counter_1 (
    .clockInput(ClockInput), .resetPin(ResetInput), .A3(SecondLSD[3]), .A2(SecondLSD[2]), .A1(SecondLSD[1]),
    .A0(SecondLSD[0]), .oneCycle(bcd_counter_1_onecycle));
  UptoFiveCounter uptofivecounter_1 (
    .clockInput(bcd_counter_1_onecycle), .resetPin(buffer_1_out), .A3(SecondMSD[3]), .A2(SecondMSD[2]),
    .A1(SecondMSD[1]), .A0(SecondMSD[0]), .oneCycle(uptofivecounter_1_onecycle));
  bcd_counter bcd_counter_2 (
    .clockInput(uptofivecounter_1_onecycle), .resetPin(buffer_2_out), .A3(MinuteLSD[3]), .A2(MinuteLSD[2]),
    .A1(MinuteLSD[1]), .A0(MinuteLSD[0]), .oneCycle(bcd_counter_2_onecycle));
  bcd_counter bcd_counter_3 (
    .clockInput(bcd_counter_2_onecycle), .resetPin(buffer_3_out), .A3(MinuteMSD[3]), .A2(MinuteMSD[2]),
    .A1(MinuteMSD[1]), .A0(MinuteMSD[0]));  // open: oneCycle
endmodule

module SpliTimeDisplay (
  input  ClockIn,
  input  [3:0] SeondLSDIN,
  input  [3:0] SecondMSDIn,
  input  [3:0] MinuteLSDIn,
  input  [3:0] MinuteMSDIN,
  input  ResetPin,
  output [3:0] SecondLSDDisplay,
  output [3:0] SecondMSDDisplay,
  output [3:0] MinuteLSDDisplay,
  output [3:0] MinutMSDDisplay,
  output [3:0] PassSecondLSD,
  output [3:0] PassSecondMSD,
  output [3:0] MinuteLSDPass,
  output [3:0] MinuteMSDPass,
  output ClockOut
);

  FourBitDFF fourbitdff_1 (
    .Clock(ClockIn), .D0(SeondLSDIN[0]), .D1(SeondLSDIN[1]), .D2(SeondLSDIN[2]), .D3(SeondLSDIN[3]),
    .ResetPin(ResetPin), .Q(SecondLSDDisplay));
  FourBitDFF fourbitdff_2 (
    .Clock(ClockIn), .D0(SecondMSDIn[0]), .D1(SecondMSDIn[1]), .D2(SecondMSDIn[2]), .D3(SecondMSDIn[3]),
    .ResetPin(ResetPin), .Q(SecondMSDDisplay));
  FourBitDFF fourbitdff_3 (
    .Clock(ClockIn), .D0(MinuteLSDIn[0]), .D1(MinuteLSDIn[1]), .D2(MinuteLSDIn[2]), .D3(MinuteLSDIn[3]),
    .ResetPin(ResetPin), .Q(MinuteLSDDisplay));
  FourBitDFF fourbitdff_4 (
    .Clock(ClockIn), .D0(MinuteMSDIN[0]), .D1(MinuteMSDIN[1]), .D2(MinuteMSDIN[2]), .D3(MinuteMSDIN[3]),
    .ResetPin(ResetPin), .Q(MinutMSDDisplay));
  FourBitDFF fourbitdff_5 (
    .Clock(ClockIn), .D0(SecondLSDDisplay[0]), .D1(SecondLSDDisplay[1]), .D2(SecondLSDDisplay[2]),
    .D3(SecondLSDDisplay[3]), .ResetPin(ResetPin), .Q(PassSecondLSD));
  FourBitDFF fourbitdff_6 (
    .Clock(ClockIn), .D0(SecondMSDDisplay[0]), .D1(SecondMSDDisplay[1]), .D2(SecondMSDDisplay[2]),
    .D3(SecondMSDDisplay[3]), .ResetPin(ResetPin), .Q(PassSecondMSD));
  FourBitDFF fourbitdff_7 (
    .Clock(ClockIn), .D0(MinuteLSDDisplay[0]), .D1(MinuteLSDDisplay[1]), .D2(MinuteLSDDisplay[2]),
    .D3(MinuteLSDDisplay[3]), .ResetPin(ResetPin), .Q(MinuteLSDPass));
  FourBitDFF fourbitdff_8 (
    .Clock(ClockIn), .D0(MinutMSDDisplay[0]), .D1(MinutMSDDisplay[1]), .D2(MinutMSDDisplay[2]),
    .D3(MinutMSDDisplay[3]), .ResetPin(ResetPin), .Q(MinuteMSDPass));

  assign ClockOut = ClockIn;
endmodule

module FourBitDFF (
  input  Clock,
  input  D0,
  input  D1,
  input  D2,
  input  D3,
  input  ResetPin,
  output [3:0] Q
);

  D_Flip_Flop d_ff_1 (.D(D0), .clk(Clock), .Q(Q[0]), .reset(ResetPin));  // open: Qn, preset
  D_Flip_Flop d_ff_2 (.D(D1), .clk(Clock), .Q(Q[1]), .reset(ResetPin));  // open: Qn, preset
  D_Flip_Flop d_ff_3 (.D(D2), .clk(Clock), .Q(Q[2]), .reset(ResetPin));  // open: Qn, preset
  D_Flip_Flop d_ff_4 (.D(D3), .clk(Clock), .Q(Q[3]), .reset(ResetPin));  // open: Qn, preset
endmodule

module digitChooser (
  input  watchState,
  input  [3:0] startDigit,
  input  [3:0] stopDigit,
  input  wrap,
  output [3:0] outDigit
);

  FourBitDFF fourbitdff_1 (
    .Clock(wrap), .D0(startDigit[0]), .D1(startDigit[1]), .D2(startDigit[2]), .D3(startDigit[3]), .Q(outDigit));  // open: ResetPin
endmodule
